# Fritzing sketch extruder (saved by Fritzing 0.9.6b)
permaprotos: 1

parts:
  Pololu_A1 = Pololu A4988 [package=SO16]  # not connected
  Part1 = Arduino Nano (Rev3.0)  # not connected
  R1 = Resistor [tolerance=±5% power=0.25 resistance=10k package=THT]  # not connected
  R2 = Resistor [tolerance=±5% power=0.25 resistance=10k package=THT]  # not connected
  BUTTON1 = Arcade Button (blue)  # not connected
  BUTTON2 = Arcade Button (green)  # not connected
  BUTTON3 = Arcade Button (red)
  R3 = Resistor [tolerance=±5% power=0.25 resistance=10k package=THT]
  M1 = Stepper Motor - Bipolar  # not connected
  C1 = Electrolytic Capacitor [capacitance=1µF voltage=35V package="100 mil [THT, electrolytic]"]  # not connected
  R4 = Rotary Potentiometer (Small) [maximum_resistance=10kΩ package=THT]  # not connected
  U1 = SLIDER [package=slider]  # not connected
  RPD-60B1 = RPD-60B
  F1 = FUSE [package=fuse_5mm]
  U2 = SWITCH-SPST-2 [package=switch-spst-vertical]

nets:
  N1: BUTTON3.no_name_yet#2, R3.Pin_1
  N2: RPD-60B1.1_(AC/N), U2.O
  N3: RPD-60B1.3_(AC/L), F1.1
  N4: F1.2, U2.P

custom parts:
  Arcade Button (blue): Adafruit Arcade Button (blue)
  Arcade Button (green): Adafruit Arcade Button (green)
  Arcade Button (red): Adafruit Arcade Button (red)
  RPD-60B: AC-DC 120V to 5V & 24V Dual output Step-Down Power Supply Module

// code stored in the sketch: extruder.ino
// Extruder controller with small NEMA 17 stepper motor and A4988 driver

// defines pins numbers
const int stepPin = 3; 
const int dirPin = 4; 
const int stopPin = 5;
const int forwardPin = 2;
const int reversePin = 1;
const int durationPin = A1;
const int speedPin = A2;
const int FORWARD = LOW;
const int REVERSE = HIGH;
const int MICROSTEPS = 16;
bool isRotating = false;
int speed = 30; // RPM
int duration = 5; // sec

void setup() {
  pinMode(stopPin, INPUT);
  pinMode(stepPin, OUTPUT);
  pinMode(dirPin, OUTPUT);
  pinMode(forwardPin, INPUT);
  pinMode(reversePin, INPUT);
  pinMode(LED_BUILTIN, OUTPUT);
};
void rotate_for_duration(int direction, int speed, int duration);
void step(int direction);

void loop() {
  digitalWrite(LED_BUILTIN, HIGH);
  speed = 20 + 100 * (analogRead(speedPin) / 1023.0);
  duration = 5 + 115 * (analogRead(durationPin) / 1023.0);

  if (digitalRead(forwardPin) && !isRotating) rotate_for_duration(FORWARD, speed, duration);
  if (digitalRead(reversePin) && !isRotating) rotate_for_duration(REVERSE, 120, 10);
}

void rotate_for_duration(int direction, int speed, int duration) {
  // speed in RPM
  if (speed < 20) speed = 20;
  if (speed > 120) speed = 120;
  // duration in sec
  if (duration < 0) return;
  if (duration > 60) duration = 60;

  isRotating = true;
  unsigned long startTime = millis(); // Record the start time
  while (millis() - startTime < duration * 1000) {
    if (!(digitalRead(stopPin))) {
      isRotating = false;
      return;
    }
    step(direction);
    // 200 * MICROSTEPS steps per revolution
    delayMicroseconds(60 * 1000 * 1000 / speed / (200 * MICROSTEPS));
  }
  isRotating = false;
}

void step(int direction) {
  if (!(digitalRead(stopPin))) return;
  digitalWrite(dirPin, direction);
  digitalWrite(stepPin, HIGH);
  digitalWrite(stepPin, LOW);
}
// thanks to Dejan Nedelkovski, www.HowToMechatronics.com
